// Logisim project drisc.circ as structural Verilog: 16 circuits, main circuit main
module main (
  input  in_1,
  input  in_2,
  input  in_3,
  input  in_4,
  input  in_5,
  input  in_6,
  input  [2:0] in_7
);

  wire Alu_Enable, and_1_out, and_2_out, Call, clock_1_out, d_ff_1_q, d_ff_2_q, d_ff_3_q, Get_Last_PC,
       Interrupt, Jump, Jump_Instruction, Load, Load_Immediate_High, No_Destination,
       operation_controller_1_set_condition_code, Phase1, Phase1n, Phase1s, Phase2, Phase2i, Phase2n,
       Phase2s, Phase3, Phase3i, Phase3n, Phase3s, por_1_out, por_2_out, por_3_out, por_4_out, por_5_out,
       por_6_out, Relative, Return_Instruction, Shift, Signed_Load, Store;
  wire [0:0] immediate_register_1_immediate_flag;
  wire [1:0] buffer_1_out, DataSize, Shift_Operation;
  wire [3:0] alu_1_carry_out, Alu_Operation, processor_status_word_1_cnzv_out;
  wire [4:0] immediate_register_1_shift_amount;
  wire [5:0] buffer_1_out_3;
  wire [23:0] buffer_1_out_2, register_1_q;
  wire [31:0] alu_1_result, buffer_2_out, data_input_output_1_lbus_out, data_input_output_1_pbus_out,
       immediate_register_1_high_immediate_19bit, immediate_register_1_immediate_13bit,
       program_counter_1_c_bus_out, program_counter_1_p_bus_out, program_counter_1_program_counter_out,
       RAM_MEM_data, register_file_1_a_bus_out, register_file_1_b_bus_out, shifter_circuit_1_c_bus_out;

  Clock clock_1 (.out(clock_1_out));
  POR #(.PorHighDuration(1), .porsize(2)) por_1 (.out(por_1_out));
  D_Flip_Flop d_ff_1 (.clk(clock_1_out), .D(d_ff_3_q), .Q(d_ff_1_q), .preset(por_1_out));  // open: Qn, reset
  POR #(.PorHighDuration(1), .porsize(2)) por_2 (.out(por_2_out));
  D_Flip_Flop d_ff_2 (.clk(clock_1_out), .D(d_ff_1_q), .Q(d_ff_2_q), .reset(por_1_out));  // open: Qn, preset
  D_Flip_Flop d_ff_3 (.clk(clock_1_out), .D(d_ff_2_q), .Q(d_ff_3_q), .reset(por_1_out));  // open: Qn, preset
  Clock_Circuit clock_circuit_1 (
    .Phase3_in(d_ff_3_q), .Load_Store_Instruction(in_3), .Window_Overflow(in_2),
    .Return_Interrupt_Instruction(Interrupt), .Interrupt(in_1), .Reset(por_2_out), .Phase1_In(d_ff_1_q),
    .Phase2_In(d_ff_2_q), .Phase3(Phase3), .Phase3i(Phase3i), .Phase3n(Phase3n), .Phase3s(Phase3s),
    .Phase1(Phase1), .Phase1n(Phase1n), .Phase1s(Phase1s), .Phase2(Phase2), .Phase2i(Phase2i),
    .Phase2n(Phase2n), .Phase2s(Phase2s));
  POR #(.PorHighDuration(1), .porsize(2)) por_3 (.out(por_3_out));
  and and_1 (and_1_out, ~No_Destination, Phase3n);  // AND_Gate
  Register_File register_file_1 (
    .C_Bus_In(buffer_2_out), .P_Bus_in({buffer_1_out_3, buffer_1_out_2, buffer_1_out}), .Phase2n(Phase2n),
    .Reset(por_3_out), .Phase2s(Phase2s), .Phase1n(Phase1n), .Phase3n(and_1_out), .Window_Number(in_7),
    .A_Bus_Out(register_file_1_a_bus_out), .B_Bus_Out(register_file_1_b_bus_out));
  // Probe on {buffer_1_out_3, buffer_1_out_2, buffer_1_out}
  // Probe on register_file_1_a_bus_out
  // Probe on register_file_1_b_bus_out
  // Probe on buffer_2_out
  assign {buffer_1_out_3, buffer_1_out_2, buffer_1_out} = data_input_output_1_pbus_out;  // Buffer buffer_1, 32 bits wide
  Data_Input_Output data_input_output_1 (
    .Data_Size(DataSize), .Load(Load), .Store(Store), .LBus_In(data_input_output_1_lbus_out),
    .PBus_In(data_input_output_1_pbus_out), .Phase1s(Phase1s), .Phase2s(Phase2s), .Signed_Data(Signed_Load),
    .Lbus_Out(data_input_output_1_lbus_out), .PBus_Out(data_input_output_1_pbus_out));
  POR #(.PorHighDuration(1), .porsize(2)) por_4 (.out(por_4_out));
  Shifter_Circuit shifter_circuit_1 (
    .Phi3n(Phase3n), .Select_Immediate(immediate_register_1_immediate_flag[0]),
    .B_Bus_In(register_file_1_b_bus_out), .Immediate_In(immediate_register_1_shift_amount),
    .Byte_Control_In(DataSize), .Load(Load), .Store(Store), .Shift(Shift),
    .A_Bus_In(register_file_1_a_bus_out), .LBus_In(data_input_output_1_lbus_out), .Phi1(Phase1),
    .Operation_Select(Shift_Operation), .Phi2(Phase2), .C_Bus_Out(shifter_circuit_1_c_bus_out),
    .LBus_Out(data_input_output_1_lbus_out));
  assign buffer_2_out = shifter_circuit_1_c_bus_out;  // Buffer buffer_2, 32 bits wide
  // Probe on shifter_circuit_1_c_bus_out
  Processor_Status_Word processor_status_word_1 (
    .LBus_in(data_input_output_1_lbus_out), .CNZV_in(alu_1_carry_out),
    .Set_Condition_Code(operation_controller_1_set_condition_code), .Enable_Write(Phase3n),
    .Reset(por_4_out), .Lbus_out(data_input_output_1_lbus_out), .CNZV_out(processor_status_word_1_cnzv_out));  // open: Enable_Lbus_Out
  Immediate_Register immediate_register_1 (
    .Pbus_In({buffer_1_out_3, buffer_1_out_2, buffer_1_out}), .Write_Enable(Phase2n),
    .Immediate_13bit(immediate_register_1_immediate_13bit),
    .High_Immediate_19bit(immediate_register_1_high_immediate_19bit),
    .Shift_Amount(immediate_register_1_shift_amount), .Immediate_Flag(immediate_register_1_immediate_flag[0]));
  ALU alu_1 (
    .Phase2(Phase2), .Phase3(Phase3), .Enable_Output(Alu_Enable), .Source2(register_file_1_b_bus_out),
    .Immediate_13bit(immediate_register_1_immediate_13bit), .Input_Select1({1'b0, Relative}),
    .Source1(register_file_1_a_bus_out), .Program_Counter_In(program_counter_1_program_counter_out),
    .Input_Select2({Load_Immediate_High, immediate_register_1_immediate_flag[0]}),
    .High_Immediate_19bit(immediate_register_1_high_immediate_19bit), .Phase1(Phase1),
    .Carry_In(processor_status_word_1_cnzv_out[3]), .Operation(Alu_Operation), .Negative(alu_1_carry_out[1]),
    .Overflow(alu_1_carry_out[3]), .Carry_Out(alu_1_carry_out[0]), .Zero(alu_1_carry_out[2]),
    .Result(alu_1_result));  // open: Result_Negated
  // Probe on Alu_Operation
  // Probe on alu_1_result
  assign buffer_2_out = alu_1_result;  // Buffer buffer_3, 32 bits wide
  // Probe on alu_1_carry_out
  Operation_Controller operation_controller_1 (
    .P_Bus_In({buffer_1_out_3, buffer_1_out_2, buffer_1_out}), .Phase2n(Phase2n), .Phase1(Phase1),
    .Phase3n(Phase3n), .CNZV_In(processor_status_word_1_cnzv_out), .Reset(por_5_out),
    .Set_Condition_Code(operation_controller_1_set_condition_code), .Data_Size(DataSize),
    .Shift_Operation(Shift_Operation), .Shift(Shift), .Load_Immediate_High(Load_Immediate_High),
    .ALU_Enabled(Alu_Enable), .ALU_Operation(Alu_Operation), .Get_Last_Program_Counter(Get_Last_PC),
    .Call(Call), .Return_Instruction(Return_Instruction), .Relative(Relative), .Interrupt(Interrupt),
    .No_Destination(No_Destination), .Load(Load), .Store(Store), .Signed_Load(Signed_Load),
    .Jump_Instruction(Jump_Instruction), .Jump(Jump));  // open: Phase2, Phase3, Phase1n, Phase1s, Phase2s, Phase3s, Phase2i, Phase3i
  POR #(.PorHighDuration(1), .porsize(2)) por_5 (.out(por_5_out));
  Program_Counter program_counter_1 (
    .Enable_Current_Out(in_5), .Enable_Last_Out(Get_Last_PC), .Reset(in_4), .Phase2(Phase2),
    .Phase_3n(Phase3n), .Phase_3i(Phase3i), .Phase1n(Phase1n), .D_Bus_In(alu_1_result), .Jump(Jump),
    .D_Bus_To_P(in_6), .Phase2n(Phase2n), .P_Bus_Out(program_counter_1_p_bus_out),
    .Program_Counter_Out(program_counter_1_program_counter_out), .C_Bus_Out(program_counter_1_c_bus_out));
  assign {buffer_1_out_3, buffer_1_out_2, buffer_1_out} = program_counter_1_p_bus_out;  // Buffer buffer_4, 32 bits wide
  // Probe on program_counter_1_c_bus_out
  assign buffer_2_out = program_counter_1_c_bus_out;  // Buffer buffer_5, 32 bits wide
  assign {buffer_1_out_3, buffer_1_out_2, buffer_1_out} = RAM_MEM_data;  // Buffer buffer_6, 32 bits wide
  Register #(.trigger("high"), .width(24)) register_1 (
    .D(buffer_1_out_2), .en(Phase1n), .clk(Phase1n), .Q(register_1_q), .clr(por_6_out));
  and and_2 (and_2_out, Store, Phase2n);
  POR #(.PorHighDuration(1), .porsize(2)) por_6 (.out(por_6_out));
  // Probe on RAM_MEM_data
  RAM #(.addrWidth(24), .dataWidth(32), .databus("bidir"), .trigger("high"), .\type ("nonvolatile")) RAM_MEM (
    .addr(register_1_q), .we(and_2_out), .oe(Phase2n), .data(RAM_MEM_data));

  // Notes on the sheet:
  //   Program Counter(Dline)
endmodule

module Clock_Circuit (
  input  Interrupt,
  input  Reset,
  input  Phase1_In,
  input  Phase2_In,
  input  Phase3_in,
  input  Load_Store_Instruction,
  input  Window_Overflow,
  input  Return_Interrupt_Instruction,
  output Phase2n,
  output Phase1,
  output Phase1s,
  output Phase2,
  output Phase3,
  output Phase3n,
  output Phase2s,
  output Phase1n,
  output Phase2i,
  output Phase3i,
  output Phase3s
);

  wire and_1_out, and_2_out, and_8_out, and_12_out, Interrupt_Enable_q, Interruption_q, not_1_out, not_2_out,
       not_3_out, or_1_out, or_2_out, SecondaryA_q, SecondaryB_q;

  and and_1 (and_1_out, Return_Interrupt_Instruction, Phase3n);
  or or_1 (or_1_out, Interrupt, Window_Overflow);
  Register #(.trigger("high"), .width(1)) Interrupt_Enable (
    .D(and_1_out), .en(and_1_out), .clk(1'b1), .Q(Interrupt_Enable_q), .clr(Phase2i));
  and and_2 (and_2_out, or_1_out, Interrupt_Enable_q);
  or or_2 (or_2_out, Reset, and_2_out);
  and and_3 (Phase1n, not_2_out, Phase1_In);
  and and_4 (Phase1s, SecondaryA_q, Phase1_In);
  Register #(.trigger("high"), .width(1)) Interruption (
    .D(or_2_out), .en(Phase1_In), .clk(Phase1_In), .Q(Interruption_q));  // open: clr
  not not_1 (not_1_out, Interruption_q);
  and and_5 (Phase2i, Interruption_q, Phase2_In);
  and and_6 (Phase2n, not_3_out, not_1_out, Phase2_In);
  and and_7 (Phase2s, SecondaryB_q, not_1_out, Phase2_In);
  Register #(.trigger("high"), .width(1)) SecondaryA (
    .D(and_8_out), .en(Phase2_In), .clk(Phase2_In), .Q(SecondaryA_q));  // open: clr
  and and_8 (and_8_out, Load_Store_Instruction, not_3_out);
  not not_2 (not_2_out, SecondaryA_q);
  and and_9 (Phase3i, Interruption_q, Phase3_in);
  and and_10 (Phase3n, not_2_out, not_1_out, Phase3_in);
  and and_11 (Phase3s, SecondaryA_q, not_1_out, Phase3_in);
  Register #(.trigger("high"), .width(1)) SecondaryB (
    .D(and_12_out), .en(Phase3_in), .clk(Phase3_in), .Q(SecondaryB_q));  // open: clr
  and and_12 (and_12_out, not_1_out, SecondaryA_q);
  not not_3 (not_3_out, SecondaryB_q);

  assign Phase1 = Phase1_In;
  assign Phase2 = Phase2_In;
  assign Phase3 = Phase3_in;
endmodule

module ALU (
  input  [3:0] Operation,
  input  Phase1,
  input  Phase3,
  input  Enable_Output,
  input  Carry_In,
  input  Phase2,
  input  [1:0] Input_Select1,
  input  [31:0] Source1,
  input  [31:0] Program_Counter_In,
  input  [1:0] Input_Select2,
  input  [31:0] Source2,
  input  [31:0] Immediate_13bit,
  input  [31:0] High_Immediate_19bit,
  output [31:0] Result,
  output [31:0] Result_Negated,
  output Zero,
  output Negative,
  output Overflow,
  output Carry_Out
);

  wire adder_1_cout, and_1_out, and_3_out, subtractor_1_bout;
  wire [30:0] C_q;
  wire [31:0] adder_1_out, and_2_out, multiplexer_1_out, multiplexer_2_out, multiplexer_3_out,
       multiplexer_4_out, multiplexer_6_out, not_1_out, or_1_out, S1_q, S2_q, subtractor_1_out, xor_1_out;

  Multiplexer #(.select(2), .width(32)) multiplexer_1 (
    .in0(Source1), .in1(Source1), .in2(Program_Counter_In), .in3({32{1'b0}}), .out(multiplexer_1_out),
    .sel(Input_Select1));
  Multiplexer #(.select(2), .width(32)) multiplexer_2 (
    .in0(Source2), .in1(Immediate_13bit), .in2(High_Immediate_19bit), .in3(High_Immediate_19bit),
    .out(multiplexer_2_out), .sel(Input_Select2));
  Register #(.trigger("high"), .width(32)) S1 (
    .D(multiplexer_1_out), .en(Phase1), .clk(Phase1), .Q(S1_q));  // open: clr
  Register #(.trigger("high"), .width(32)) S2 (
    .D(multiplexer_2_out), .en(Phase1), .clk(Phase1), .Q(S2_q));  // open: clr
  // Probe on S1_q
  // Probe on S2_q
  Multiplexer #(.width(32)) multiplexer_3 (.in0(S1_q), .in1(S2_q), .out(multiplexer_3_out), .sel(Operation[3]));
  Multiplexer #(.width(32)) multiplexer_4 (.in0(S2_q), .in1(S1_q), .out(multiplexer_4_out), .sel(Operation[3]));
  and and_1 (and_1_out, Carry_In, Operation[0]);
  assign and_2_out = multiplexer_3_out & multiplexer_4_out;  // AND_Gate and_2, 32 bits wide
  assign xor_1_out = multiplexer_3_out ^ multiplexer_4_out;  // XOR_Gate xor_1, 32 bits wide
  assign or_1_out = multiplexer_3_out | multiplexer_4_out;  // OR_Gate or_1, 32 bits wide
  Subtractor #(.width(32)) subtractor_1 (
    .a(multiplexer_3_out), .b(multiplexer_4_out), .out(subtractor_1_out), .bin(and_1_out),
    .bout(subtractor_1_bout));
  Adder #(.width(32)) adder_1 (
    .a(multiplexer_3_out), .b(multiplexer_4_out), .out(adder_1_out), .cin(and_1_out), .cout(adder_1_cout));
  Multiplexer multiplexer_5 (.in0(subtractor_1_bout), .in1(adder_1_cout), .out(Carry_Out), .sel(Operation[1]));
  Multiplexer #(.select(3), .width(32)) multiplexer_6 (
    .in0(multiplexer_4_out), .in1(and_2_out), .in2(xor_1_out), .in3(or_1_out), .in4(subtractor_1_out),
    .in5(subtractor_1_out), .in6(adder_1_out), .in7(adder_1_out), .out(multiplexer_6_out),
    .sel(Operation[2:0]));
  Register #(.trigger("high"), .width(32)) C (
    .D(multiplexer_6_out), .en(Phase2), .clk(Phase2), .Q({Negative, C_q}));  // open: clr
  assign not_1_out = ~{Negative, C_q};  // NOT_Gate not_1, 32 bits wide
  nor nor_1 (Zero, C_q[0], C_q[1], C_q[2], C_q[3], C_q[4], C_q[5], C_q[6], C_q[7], C_q[8], C_q[9], C_q[10], C_q[11], C_q[12], C_q[13], C_q[14], C_q[15], C_q[16], C_q[17], C_q[18], C_q[19], C_q[20], C_q[21], C_q[22], C_q[23], C_q[24], C_q[25], C_q[26], C_q[27], C_q[28], C_q[29], C_q[30], Negative);
  xor xor_2 (Overflow, Negative, Carry_Out);
  assign Result_Negated = and_3_out ? not_1_out : 32'bz;  // Controlled_Buffer controlled_buffer_1
  and and_3 (and_3_out, Phase3, Enable_Output);
  assign Result = and_3_out ? {Negative, C_q} : 32'bz;  // Controlled_Buffer controlled_buffer_2

  // Notes on the sheet:
  //   Source1: initial=0xffffffff
endmodule

module Program_Counter (
  input  Phase2n,
  input  Phase2,
  input  Reset,
  input  Enable_Current_Out,
  input  Enable_Last_Out,
  input  Phase1n,
  input  [31:0] D_Bus_In,
  input  Jump,
  input  D_Bus_To_P,
  input  Phase_3n,
  input  Phase_3i,
  output [31:0] Program_Counter_Out,
  output [31:0] C_Bus_Out,
  output [31:0] P_Bus_Out
);

  wire and_1_out, or_1_out;
  wire [29:0] adder_1_out, controlled_buffer_1_out, Last_q, Output_Latch_q, register_1_q;

  Adder #(.width(30)) adder_1 (.a(register_1_q), .b(30'h1), .out(adder_1_out));  // open: cin, cout
  Register #(.trigger("high"), .width(30)) Output_Latch (
    .D(adder_1_out), .en(Phase2), .clk(Phase2), .Q(Output_Latch_q), .clr(Reset));
  or or_1 (or_1_out, Phase_3n, Phase_3i);
  assign controlled_buffer_1_out = Jump ? D_Bus_In[29:0] : 30'bz;  // Controlled_Buffer controlled_buffer_1
  assign controlled_buffer_1_out = and_1_out ? Output_Latch_q : 30'bz;  // Controlled_Buffer controlled_buffer_2
  and and_1 (and_1_out, ~Jump, Phase_3n);  // AND_Gate
  Register #(.trigger("high"), .width(30)) register_1 (
    .D(controlled_buffer_1_out), .en(or_1_out), .clk(or_1_out), .Q(register_1_q), .clr(Reset));
  assign P_Bus_Out[31:2] = D_Bus_To_P ? controlled_buffer_1_out : 30'bz;  // Controlled_Buffer controlled_buffer_3
  assign P_Bus_Out[31:2] = Phase1n ? register_1_q : 30'bz;  // Controlled_Buffer controlled_buffer_4
  assign P_Bus_Out[31:2] = Phase_3i ? {30{1'b0}} : 30'bz;  // Controlled_Buffer Interrupt_Vector
  Register #(.width(30)) Current (
    .D(register_1_q), .en(Phase2n), .clk(Phase2n), .Q(Program_Counter_Out[31:2]), .clr(Reset));
  assign C_Bus_Out = Enable_Current_Out ? {Program_Counter_Out[31:2], 2'b00} : 32'bz;  // Controlled_Buffer controlled_buffer_5
  Register #(.width(30)) Last (.D(Program_Counter_Out[31:2]), .en(Phase1n), .clk(Phase1n), .Q(Last_q), .clr(Reset));
  assign C_Bus_Out = Enable_Last_Out ? {Last_q, 2'b00} : 32'bz;  // Controlled_Buffer controlled_buffer_6

  assign Program_Counter_Out[1:0] = 2'b00;

  // Notes on the sheet:
  //   Next
endmodule

module Immediate_Register (
  input  [31:0] Pbus_In,
  input  Write_Enable,
  output [4:0] Shift_Amount,
  output Immediate_Flag,
  output [31:0] Immediate_13bit,
  output [31:0] High_Immediate_19bit
);

  Register #(.trigger("high"), .width(19)) register_1 (
    .D(Pbus_In[31:13]), .en(Write_Enable), .clk(1'b1), .Q(High_Immediate_19bit[31:13]));  // open: clr
  assign Immediate_13bit = {{19{High_Immediate_19bit[31]}}, High_Immediate_19bit[31:19]};  // Bit_Extender bit_extender_1

  assign High_Immediate_19bit[12:0] = {13{1'b0}};
  assign Immediate_Flag = High_Immediate_19bit[18];
  assign Shift_Amount = High_Immediate_19bit[17:13];
endmodule

module Data_Input_Output (
  input  Phase1s,
  input  Phase2s,
  input  Signed_Data,
  input  [1:0] Data_Size,
  input  Load,
  input  Store,
  input  [31:0] PBus_In,
  input  [31:0] LBus_In,
  output [31:0] PBus_Out,
  output [31:0] Lbus_Out
);

  wire and_1_out, and_2_out, and_3_out, and_4_out, and_5_out, or_1_out;
  wire [7:0] bit_extender_1_out, bit_extender_2_out, bit_extender_3_out, multiplexer_1_out,
       multiplexer_2_out, multiplexer_3_out, multiplexer_4_out, multiplexer_5_out, multiplexer_6_out,
       multiplexer_7_out, register_1_q, register_2_q, register_3_q, register_4_q;
  wire [31:0] controlled_buffer_2_out, controlled_buffer_7_out;

  assign PBus_Out = Phase2s ? controlled_buffer_2_out : 32'bz;  // Controlled_Buffer controlled_buffer_1
  assign controlled_buffer_2_out = Phase1s ? PBus_In : 32'bz;  // Controlled_Buffer controlled_buffer_2
  assign controlled_buffer_2_out[7:0] = Phase2s ? register_1_q : 8'bz;  // Controlled_Buffer controlled_buffer_3
  assign controlled_buffer_2_out[15:8] = Phase2s ? register_2_q : 8'bz;  // Controlled_Buffer controlled_buffer_4
  assign controlled_buffer_2_out[23:16] = Phase2s ? register_3_q : 8'bz;  // Controlled_Buffer controlled_buffer_5
  assign controlled_buffer_2_out[31:24] = Phase2s ? register_4_q : 8'bz;  // Controlled_Buffer controlled_buffer_6
  Multiplexer #(.width(8)) multiplexer_1 (
    .in0(controlled_buffer_2_out[7:0]), .in1(controlled_buffer_7_out[7:0]), .out(multiplexer_1_out),
    .sel(and_5_out));
  Multiplexer #(.width(8)) multiplexer_2 (
    .in0(controlled_buffer_2_out[15:8]), .in1(controlled_buffer_7_out[15:8]), .out(multiplexer_2_out),
    .sel(and_5_out));
  Multiplexer #(.width(8)) multiplexer_3 (
    .in0(controlled_buffer_2_out[23:16]), .in1(controlled_buffer_7_out[23:16]), .out(multiplexer_3_out),
    .sel(and_5_out));
  Multiplexer #(.width(8)) multiplexer_4 (
    .in0(controlled_buffer_2_out[31:24]), .in1(controlled_buffer_7_out[31:24]), .out(multiplexer_4_out),
    .sel(and_5_out));
  or or_1 (or_1_out, Phase1s, and_5_out);
  Register #(.trigger("high")) register_1 (
    .D(multiplexer_1_out), .en(or_1_out), .clk(or_1_out), .Q(register_1_q));  // open: clr
  Register #(.trigger("high")) register_2 (
    .D(multiplexer_2_out), .en(or_1_out), .clk(or_1_out), .Q(register_2_q));  // open: clr
  Register #(.trigger("high")) register_3 (
    .D(multiplexer_3_out), .en(or_1_out), .clk(or_1_out), .Q(register_3_q));  // open: clr
  Register #(.trigger("high")) register_4 (
    .D(multiplexer_4_out), .en(or_1_out), .clk(or_1_out), .Q(register_4_q));  // open: clr
  and and_1 (and_1_out, Signed_Data, register_1_q[7]);
  and and_2 (and_2_out, Signed_Data, multiplexer_5_out[7]);
  and and_3 (and_3_out, Signed_Data, multiplexer_6_out[7]);
  assign bit_extender_1_out = {{7{and_1_out}}, and_1_out};  // Bit_Extender bit_extender_1
  Multiplexer #(.width(8)) multiplexer_5 (
    .in0(bit_extender_1_out), .in1(register_2_q), .out(multiplexer_5_out), .sel(Data_Size[0]));
  assign bit_extender_2_out = {{7{and_2_out}}, and_2_out};  // Bit_Extender bit_extender_2
  Multiplexer #(.width(8)) multiplexer_6 (
    .in0(bit_extender_2_out), .in1(register_3_q), .out(multiplexer_6_out), .sel(Data_Size[1]));
  assign bit_extender_3_out = {{7{and_3_out}}, and_3_out};  // Bit_Extender bit_extender_3
  Multiplexer #(.width(8)) multiplexer_7 (
    .in0(bit_extender_3_out), .in1(register_4_q), .out(multiplexer_7_out), .sel(Data_Size[1]));
  assign controlled_buffer_7_out[7:0] = and_4_out ? register_1_q : 8'bz;  // Controlled_Buffer controlled_buffer_7
  assign controlled_buffer_7_out[15:8] = and_4_out ? multiplexer_5_out : 8'bz;  // Controlled_Buffer controlled_buffer_8
  assign controlled_buffer_7_out[23:16] = and_4_out ? multiplexer_6_out : 8'bz;  // Controlled_Buffer controlled_buffer_9
  assign controlled_buffer_7_out[31:24] = and_4_out ? multiplexer_7_out : 8'bz;  // Controlled_Buffer controlled_buffer_10
  and and_4 (and_4_out, Phase2s, Load);
  and and_5 (and_5_out, Phase2s, Store);
  assign Lbus_Out = and_4_out ? controlled_buffer_7_out : 32'bz;  // Controlled_Buffer controlled_buffer_11
  assign controlled_buffer_7_out = and_5_out ? LBus_In : 32'bz;  // Controlled_Buffer controlled_buffer_12

  // Notes on the sheet:
  //   LBus_In: initial=0xe3e3e3e3
  //   PBus_In: initial=0xf2f2f2f2
endmodule

module Shifter_Circuit (
  input  Load,
  input  Store,
  input  Shift,
  input  Phi3n,
  input  Select_Immediate,
  input  [31:0] B_Bus_In,
  input  [4:0] Immediate_In,
  input  [1:0] Byte_Control_In,
  input  [1:0] Operation_Select,
  input  Phi1,
  input  [31:0] A_Bus_In,
  input  Phi2,
  input  [31:0] LBus_In,
  output [31:0] C_Bus_Out,
  output [31:0] LBus_Out
);

  wire and_1_out, or_1_out, or_2_out, or_3_out;
  wire [4:0] multiplexer_1_out, multiplexer_2_out, Shift_Amount_Latch_q;
  wire [31:0] controlled_buffer_1_out, multiplexer_3_out, Shift_In_Latch_q, Shift_Out_Latch_q, shifter_1_out,
       shifter_2_out, shifter_3_out;

  Multiplexer #(.width(5)) multiplexer_1 (
    .in0(B_Bus_In[4:0]), .in1(Immediate_In), .out(multiplexer_1_out), .sel(Select_Immediate));
  or or_1 (or_1_out, Load, Store);
  Multiplexer #(.width(5)) multiplexer_2 (
    .in0(multiplexer_1_out), .in1({Byte_Control_In, 3'b000}), .out(multiplexer_2_out), .sel(or_1_out));
  assign controlled_buffer_1_out = Load ? LBus_In : 32'bz;  // Controlled_Buffer controlled_buffer_1
  assign LBus_Out = Store ? controlled_buffer_1_out : 32'bz;  // Controlled_Buffer controlled_buffer_2
  Register #(.trigger("high"), .width(5)) Shift_Amount_Latch (
    .D(multiplexer_2_out), .en(Phi1), .clk(Phi1), .Q(Shift_Amount_Latch_q));  // open: clr
  Register #(.trigger("high"), .width(32)) Shift_In_Latch (
    .D(A_Bus_In), .en(Phi1), .clk(Phi1), .Q(Shift_In_Latch_q));  // open: clr
  or or_2 (or_2_out, Shift, Store);
  assign controlled_buffer_1_out = or_2_out ? Shift_In_Latch_q : 32'bz;  // Controlled_Buffer controlled_buffer_3
  Shifter #(.width(32)) shifter_1 (.in(controlled_buffer_1_out), .\dist (Shift_Amount_Latch_q), .out(shifter_1_out));
  Shifter #(.shift("lr"), .width(32)) shifter_2 (
    .in(controlled_buffer_1_out), .\dist (Shift_Amount_Latch_q), .out(shifter_2_out));
  Shifter #(.shift("ar"), .width(32)) shifter_3 (
    .in(controlled_buffer_1_out), .\dist (Shift_Amount_Latch_q), .out(shifter_3_out));
  Multiplexer #(.select(2), .width(32)) multiplexer_3 (
    .in0(shifter_1_out), .in1(shifter_2_out), .in2(shifter_3_out), .in3(shifter_3_out),
    .out(multiplexer_3_out), .sel(Operation_Select));
  Register #(.trigger("high"), .width(32)) Shift_Out_Latch (
    .D(multiplexer_3_out), .en(Phi2), .clk(Phi2), .Q(Shift_Out_Latch_q));  // open: clr
  or or_3 (or_3_out, Shift, Load);
  and and_1 (and_1_out, or_3_out, Phi3n);
  assign C_Bus_Out = and_1_out ? Shift_Out_Latch_q : 32'bz;  // Controlled_Buffer controlled_buffer_4
endmodule

module Register_Window (
  input  [3:0] Address_A,
  input  Read_Enable_A,
  input  Reset,
  input  [31:0] Data_In,
  input  [3:0] Address_C,
  input  Write_Enable,
  input  [3:0] Address_B,
  input  Read_Enable_B,
  output [31:0] A_Data_Out,
  output [31:0] B_Data_Out
);

  wire decoder_1_out0, decoder_1_out1, decoder_1_out2, decoder_1_out3, decoder_1_out4, decoder_1_out5,
       decoder_1_out6, decoder_1_out7, decoder_1_out8, decoder_1_out9, decoder_1_out10, decoder_1_out11,
       decoder_1_out12, decoder_1_out13, decoder_1_out14, decoder_1_out15;
  wire [31:0] Reg0_q, Reg1_q, Reg2_q, Reg3_q, Reg4_q, Reg5_q, Reg6_q, Reg7_q, Reg8_q, Reg9_q, RegA_q, RegB_q,
       RegC_q, RegD_q, RegE_q, RegF_q;

  Decoder #(.select(4)) decoder_1 (
    .out0(decoder_1_out0), .out1(decoder_1_out1), .out2(decoder_1_out2), .out3(decoder_1_out3),
    .out4(decoder_1_out4), .out5(decoder_1_out5), .out6(decoder_1_out6), .out7(decoder_1_out7),
    .out8(decoder_1_out8), .out9(decoder_1_out9), .out10(decoder_1_out10), .out11(decoder_1_out11),
    .out12(decoder_1_out12), .out13(decoder_1_out13), .out14(decoder_1_out14), .out15(decoder_1_out15),
    .sel(Address_C), .en(Write_Enable));
  Register #(.width(32)) Reg0 (.D(Data_In), .en(decoder_1_out0), .clk(decoder_1_out0), .Q(Reg0_q), .clr(Reset));
  Register #(.width(32)) Reg2 (.D(Data_In), .en(decoder_1_out2), .clk(decoder_1_out2), .Q(Reg2_q), .clr(Reset));
  Register #(.width(32)) Reg4 (.D(Data_In), .en(decoder_1_out4), .clk(decoder_1_out4), .Q(Reg4_q), .clr(Reset));
  Register #(.width(32)) Reg6 (.D(Data_In), .en(decoder_1_out6), .clk(decoder_1_out6), .Q(Reg6_q), .clr(Reset));
  Register #(.width(32)) Reg8 (.D(Data_In), .en(decoder_1_out8), .clk(decoder_1_out8), .Q(Reg8_q), .clr(Reset));
  Register #(.width(32)) RegA (.D(Data_In), .en(decoder_1_out10), .clk(decoder_1_out10), .Q(RegA_q), .clr(Reset));
  Register #(.width(32)) RegC (.D(Data_In), .en(decoder_1_out12), .clk(decoder_1_out12), .Q(RegC_q), .clr(Reset));
  Register #(.width(32)) RegE (.D(Data_In), .en(decoder_1_out14), .clk(decoder_1_out14), .Q(RegE_q), .clr(Reset));
  Register #(.width(32)) Reg1 (.D(Data_In), .en(decoder_1_out1), .clk(decoder_1_out1), .Q(Reg1_q), .clr(Reset));
  Register #(.width(32)) Reg3 (.D(Data_In), .en(decoder_1_out3), .clk(decoder_1_out3), .Q(Reg3_q), .clr(Reset));
  Register #(.width(32)) Reg5 (.D(Data_In), .en(decoder_1_out5), .clk(decoder_1_out5), .Q(Reg5_q), .clr(Reset));
  Register #(.width(32)) Reg7 (.D(Data_In), .en(decoder_1_out7), .clk(decoder_1_out7), .Q(Reg7_q), .clr(Reset));
  Register #(.width(32)) Reg9 (.D(Data_In), .en(decoder_1_out9), .clk(decoder_1_out9), .Q(Reg9_q), .clr(Reset));
  Register #(.width(32)) RegB (.D(Data_In), .en(decoder_1_out11), .clk(decoder_1_out11), .Q(RegB_q), .clr(Reset));
  Register #(.width(32)) RegD (.D(Data_In), .en(decoder_1_out13), .clk(decoder_1_out13), .Q(RegD_q), .clr(Reset));
  Register #(.width(32)) RegF (.D(Data_In), .en(decoder_1_out15), .clk(decoder_1_out15), .Q(RegF_q), .clr(Reset));
  Multiplexer #(.disabled("Z"), .enable("true"), .select(4), .width(32)) multiplexer_1 (
    .in0(Reg0_q), .in1(Reg1_q), .in2(Reg2_q), .in3(Reg3_q), .in4(Reg4_q), .in5(Reg5_q), .in6(Reg6_q),
    .in7(Reg7_q), .in8(Reg8_q), .in9(Reg9_q), .in10(RegA_q), .in11(RegB_q), .in12(RegC_q), .in13(RegD_q),
    .in14(RegE_q), .in15(RegF_q), .out(A_Data_Out), .sel(Address_A), .en(Read_Enable_A));
  Multiplexer #(.disabled("Z"), .enable("true"), .select(4), .width(32)) multiplexer_2 (
    .in0(Reg0_q), .in1(Reg1_q), .in2(Reg2_q), .in3(Reg3_q), .in4(Reg4_q), .in5(Reg5_q), .in6(Reg6_q),
    .in7(Reg7_q), .in8(Reg8_q), .in9(Reg9_q), .in10(RegA_q), .in11(RegB_q), .in12(RegC_q), .in13(RegD_q),
    .in14(RegE_q), .in15(RegF_q), .out(B_Data_Out), .sel(Address_B), .en(Read_Enable_B));
endmodule

module Register_File (
  input  Phase2n,
  input  Phase2s,
  input  [31:0] P_Bus_in,
  input  [31:0] C_Bus_In,
  input  [2:0] Window_Number,
  input  Reset,
  input  Phase1n,
  input  Phase3n,
  output [31:0] A_Bus_Out,
  output [31:0] B_Bus_Out
);

  wire or_1_out, or_2_out;
  wire [2:0] A_Address_q_2, and_1_out, cwp_and_address_decoder_1_decoded_enables,
       cwp_and_address_decoder_1_decoded_enables_2, cwp_and_address_decoder_1_decoded_enables_3,
       cwp_and_address_decoder_1_decoded_enables_4, cwp_and_address_decoder_1_decoded_enables_5,
       cwp_and_address_decoder_1_decoded_enables_6, cwp_and_address_decoder_1_decoded_enables_7,
       cwp_and_address_decoder_1_decoded_enables_8;
  wire [3:0] A_Address_q, B_Address_q, C_Address_q;
  wire [4:0] multiplexer_1_out, Next_A_q, Next_B_q, Next_C_q;

  or or_1 (or_1_out, Phase2n, Phase2s);
  Register #(.trigger("high"), .width(5)) Next_A (
    .D(P_Bus_in[17:13]), .en(or_1_out), .clk(or_1_out), .Q(Next_A_q), .clr(Reset));
  Register #(.trigger("high"), .width(5)) Next_B (
    .D(P_Bus_in[31:27]), .en(or_1_out), .clk(or_1_out), .Q(Next_B_q), .clr(Reset));
  Register #(.trigger("high"), .width(5)) Next_C (
    .D(P_Bus_in[12:8]), .en(or_1_out), .clk(or_1_out), .Q(Next_C_q), .clr(Reset));
  Multiplexer #(.width(5)) multiplexer_1 (.in0(Next_A_q), .in1(Next_C_q), .out(multiplexer_1_out), .sel(Phase2s));
  Register #(.width(5)) A_Address (
    .D(multiplexer_1_out), .en(or_2_out), .clk(or_2_out), .Q({A_Address_q_2[0], A_Address_q}), .clr(Reset));
  or or_2 (or_2_out, Phase2s, Phase1n);
  Register #(.width(5)) B_Address (
    .D(Next_B_q), .en(Phase1n), .clk(Phase1n), .Q({A_Address_q_2[1], B_Address_q}), .clr(Reset));
  Register #(.width(5)) C_Address (
    .D(Next_C_q), .en(Phase1n), .clk(Phase1n), .Q({A_Address_q_2[2], C_Address_q}), .clr(Reset));
  CWP_And_Address_Decoder cwp_and_address_decoder_1 (
    .A_Address({A_Address_q_2[0], A_Address_q}), .B_Address({A_Address_q_2[1], B_Address_q}),
    .C_Address({A_Address_q_2[2], C_Address_q}), .Enable_Write(Phase3n), .Enable_Read(Phase1n),
    .Context_Window_Pointer(Window_Number),
    .Decoded_Enables({cwp_and_address_decoder_1_decoded_enables_8, cwp_and_address_decoder_1_decoded_enables_7, cwp_and_address_decoder_1_decoded_enables_6, cwp_and_address_decoder_1_decoded_enables_5, cwp_and_address_decoder_1_decoded_enables_4, cwp_and_address_decoder_1_decoded_enables_3, cwp_and_address_decoder_1_decoded_enables_2, cwp_and_address_decoder_1_decoded_enables}));
  assign and_1_out = ~A_Address_q_2 & {Phase3n, {2{Phase1n}}};  // AND_Gate and_1, 3 bits wide
  Register_Window register_window_1 (
    .Address_A(A_Address_q), .Address_B(B_Address_q),
    .Read_Enable_A(cwp_and_address_decoder_1_decoded_enables_8[0]),
    .Read_Enable_B(cwp_and_address_decoder_1_decoded_enables_8[1]), .Reset(Reset), .Data_In(C_Bus_In),
    .Address_C(C_Address_q), .Write_Enable(cwp_and_address_decoder_1_decoded_enables_8[2]),
    .A_Data_Out(A_Bus_Out), .B_Data_Out(B_Bus_Out));
  Register_Window register_window_2 (
    .Address_A(A_Address_q), .Address_B(B_Address_q),
    .Read_Enable_A(cwp_and_address_decoder_1_decoded_enables_6[0]),
    .Read_Enable_B(cwp_and_address_decoder_1_decoded_enables_6[1]), .Reset(Reset), .Data_In(C_Bus_In),
    .Address_C(C_Address_q), .Write_Enable(cwp_and_address_decoder_1_decoded_enables_6[2]),
    .A_Data_Out(A_Bus_Out), .B_Data_Out(B_Bus_Out));
  Register_Window register_window_3 (
    .Address_A(A_Address_q), .Address_B(B_Address_q),
    .Read_Enable_A(cwp_and_address_decoder_1_decoded_enables_4[0]),
    .Read_Enable_B(cwp_and_address_decoder_1_decoded_enables_4[1]), .Reset(Reset), .Data_In(C_Bus_In),
    .Address_C(C_Address_q), .Write_Enable(cwp_and_address_decoder_1_decoded_enables_4[2]),
    .A_Data_Out(A_Bus_Out), .B_Data_Out(B_Bus_Out));
  Register_Window register_window_4 (
    .Address_A(A_Address_q), .Address_B(B_Address_q),
    .Read_Enable_A(cwp_and_address_decoder_1_decoded_enables_2[0]),
    .Read_Enable_B(cwp_and_address_decoder_1_decoded_enables_2[1]), .Reset(Reset), .Data_In(C_Bus_In),
    .Address_C(C_Address_q), .Write_Enable(cwp_and_address_decoder_1_decoded_enables_2[2]),
    .A_Data_Out(A_Bus_Out), .B_Data_Out(B_Bus_Out));
  Global_Registers global_registers_1 (
    .Address_A(A_Address_q), .Address_B(B_Address_q), .Read_Enable_A(and_1_out[0]),
    .Read_Enable_B(and_1_out[1]), .Reset(Reset), .Data_In(C_Bus_In), .Address_C(C_Address_q),
    .Write_Enable(and_1_out[2]), .A_Data_Out(A_Bus_Out), .B_Data_Out(B_Bus_Out));
  Register_Window register_window_5 (
    .Address_A(A_Address_q), .Address_B(B_Address_q),
    .Read_Enable_A(cwp_and_address_decoder_1_decoded_enables_7[0]),
    .Read_Enable_B(cwp_and_address_decoder_1_decoded_enables_7[1]), .Reset(Reset), .Data_In(C_Bus_In),
    .Address_C(C_Address_q), .Write_Enable(cwp_and_address_decoder_1_decoded_enables_7[2]),
    .A_Data_Out(A_Bus_Out), .B_Data_Out(B_Bus_Out));
  Register_Window register_window_6 (
    .Address_A(A_Address_q), .Address_B(B_Address_q),
    .Read_Enable_A(cwp_and_address_decoder_1_decoded_enables_5[0]),
    .Read_Enable_B(cwp_and_address_decoder_1_decoded_enables_5[1]), .Reset(Reset), .Data_In(C_Bus_In),
    .Address_C(C_Address_q), .Write_Enable(cwp_and_address_decoder_1_decoded_enables_5[2]),
    .A_Data_Out(A_Bus_Out), .B_Data_Out(B_Bus_Out));
  Register_Window register_window_7 (
    .Address_A(A_Address_q), .Address_B(B_Address_q),
    .Read_Enable_A(cwp_and_address_decoder_1_decoded_enables_3[0]),
    .Read_Enable_B(cwp_and_address_decoder_1_decoded_enables_3[1]), .Reset(Reset), .Data_In(C_Bus_In),
    .Address_C(C_Address_q), .Write_Enable(cwp_and_address_decoder_1_decoded_enables_3[2]),
    .A_Data_Out(A_Bus_Out), .B_Data_Out(B_Bus_Out));
  Register_Window register_window_8 (
    .Address_A(A_Address_q), .Address_B(B_Address_q),
    .Read_Enable_A(cwp_and_address_decoder_1_decoded_enables[0]),
    .Read_Enable_B(cwp_and_address_decoder_1_decoded_enables[1]), .Reset(Reset), .Data_In(C_Bus_In),
    .Address_C(C_Address_q), .Write_Enable(cwp_and_address_decoder_1_decoded_enables[2]),
    .A_Data_Out(A_Bus_Out), .B_Data_Out(B_Bus_Out));
endmodule

module Global_Registers (
  input  [3:0] Address_A,
  input  Read_Enable_A,
  input  Reset,
  input  [31:0] Data_In,
  input  [3:0] Address_C,
  input  Write_Enable,
  input  [3:0] Address_B,
  input  Read_Enable_B,
  output [31:0] A_Data_Out,
  output [31:0] B_Data_Out
);

  wire decoder_1_out0, decoder_1_out1, decoder_1_out2, decoder_1_out3, decoder_1_out4, decoder_1_out5,
       decoder_1_out6, decoder_1_out7, decoder_1_out8, decoder_1_out9, decoder_1_out10, decoder_1_out11,
       decoder_1_out12, decoder_1_out13, decoder_1_out14, decoder_1_out15;
  wire [31:0] Reg1_q, Reg2_q, Reg3_q, Reg4_q, Reg5_q, Reg6_q, Reg7_q, Reg8_q, Reg9_q, undriven, undriven_2,
       undriven_3, undriven_4, undriven_5, undriven_6;

  Decoder #(.select(4)) decoder_1 (
    .out0(decoder_1_out0), .out1(decoder_1_out1), .out2(decoder_1_out2), .out3(decoder_1_out3),
    .out4(decoder_1_out4), .out5(decoder_1_out5), .out6(decoder_1_out6), .out7(decoder_1_out7),
    .out8(decoder_1_out8), .out9(decoder_1_out9), .out10(decoder_1_out10), .out11(decoder_1_out11),
    .out12(decoder_1_out12), .out13(decoder_1_out13), .out14(decoder_1_out14), .out15(decoder_1_out15),
    .sel(Address_C), .en(Write_Enable));
  // NoConnect on decoder_1_out15
  // NoConnect on decoder_1_out14
  // NoConnect on decoder_1_out13
  // NoConnect on decoder_1_out12
  // NoConnect on decoder_1_out11
  // NoConnect on decoder_1_out10
  // NoConnect on decoder_1_out0
  Register #(.width(32)) Reg2 (.D(Data_In), .en(decoder_1_out2), .clk(decoder_1_out2), .Q(Reg2_q), .clr(Reset));
  Register #(.width(32)) Reg4 (.D(Data_In), .en(decoder_1_out4), .clk(decoder_1_out4), .Q(Reg4_q), .clr(Reset));
  Register #(.width(32)) Reg6 (.D(Data_In), .en(decoder_1_out6), .clk(decoder_1_out6), .Q(Reg6_q), .clr(Reset));
  Register #(.width(32)) Reg8 (.D(Data_In), .en(decoder_1_out8), .clk(decoder_1_out8), .Q(Reg8_q), .clr(Reset));
  Register #(.width(32)) Reg1 (.D(Data_In), .en(decoder_1_out1), .clk(decoder_1_out1), .Q(Reg1_q), .clr(Reset));
  Register #(.width(32)) Reg3 (.D(Data_In), .en(decoder_1_out3), .clk(decoder_1_out3), .Q(Reg3_q), .clr(Reset));
  Register #(.width(32)) Reg5 (.D(Data_In), .en(decoder_1_out5), .clk(decoder_1_out5), .Q(Reg5_q), .clr(Reset));
  Register #(.width(32)) Reg7 (.D(Data_In), .en(decoder_1_out7), .clk(decoder_1_out7), .Q(Reg7_q), .clr(Reset));
  Register #(.width(32)) Reg9 (.D(Data_In), .en(decoder_1_out9), .clk(decoder_1_out9), .Q(Reg9_q), .clr(Reset));
  // NoConnect on undriven
  // NoConnect on undriven_2
  // NoConnect on undriven_3
  // NoConnect on undriven_4
  // NoConnect on undriven_5
  // NoConnect on undriven_6
  Multiplexer #(.disabled("Z"), .enable("true"), .select(4), .width(32)) multiplexer_1 (
    .in0({32{1'b0}}), .in1(Reg1_q), .in2(Reg2_q), .in3(Reg3_q), .in4(Reg4_q), .in5(Reg5_q), .in6(Reg6_q),
    .in7(Reg7_q), .in8(Reg8_q), .in9(Reg9_q), .in10(undriven), .in11(undriven_2), .in12(undriven_3),
    .in13(undriven_4), .in14(undriven_5), .in15(undriven_6), .out(A_Data_Out), .sel(Address_A),
    .en(Read_Enable_A));
  Multiplexer #(.disabled("Z"), .enable("true"), .select(4), .width(32)) multiplexer_2 (
    .in0({32{1'b0}}), .in1(Reg1_q), .in2(Reg2_q), .in3(Reg3_q), .in4(Reg4_q), .in5(Reg5_q), .in6(Reg6_q),
    .in7(Reg7_q), .in8(Reg8_q), .in9(Reg9_q), .in10(undriven), .in11(undriven_2), .in12(undriven_3),
    .in13(undriven_4), .in14(undriven_5), .in15(undriven_6), .out(B_Data_Out), .sel(Address_B),
    .en(Read_Enable_B));

  // Notes on the sheet:
  //   Reg0
endmodule

module CWP_And_Address_Decoder (
  input  [4:0] A_Address,
  input  [4:0] B_Address,
  input  [4:0] C_Address,
  input  Enable_Write,
  input  Enable_Read,
  input  [2:0] Context_Window_Pointer,
  output [23:0] Decoded_Enables
);

  wire and_1_out, and_2_out, and_3_out, and_4_out, and_5_out, and_6_out, and_7_out, and_8_out, and_9_out,
       or_1_out, or_2_out, or_3_out;
  wire [2:0] and_12_out, and_15_out, demultiplexer_1_out0, demultiplexer_1_out1, demultiplexer_1_out2,
       demultiplexer_1_out3, demultiplexer_1_out4, demultiplexer_1_out5, demultiplexer_1_out6,
       demultiplexer_1_out7, demultiplexer_2_out0, demultiplexer_2_out1, demultiplexer_2_out2,
       demultiplexer_2_out3, demultiplexer_2_out4, demultiplexer_2_out5, demultiplexer_2_out6,
       demultiplexer_2_out7, subtractor_1_out;

  or or_1 (or_1_out, A_Address[1], A_Address[2]);
  and and_1 (and_1_out, A_Address[3], ~A_Address[4]);  // AND_Gate
  or or_2 (or_2_out, B_Address[1], B_Address[2]);
  and and_2 (and_2_out, B_Address[3], ~B_Address[4]);  // AND_Gate
  or or_3 (or_3_out, C_Address[1], C_Address[2]);
  and and_3 (and_3_out, C_Address[3], ~C_Address[4]);  // AND_Gate
  and and_4 (and_4_out, or_1_out, and_1_out);
  and and_5 (and_5_out, or_2_out, and_2_out);
  and and_6 (and_6_out, or_3_out, and_3_out);
  Subtractor #(.width(3)) subtractor_1 (
    .a(Context_Window_Pointer), .b(3'b001), .out(subtractor_1_out));  // open: bin, bout
  and and_7 (and_7_out, A_Address[4], ~and_4_out);  // AND_Gate
  and and_8 (and_8_out, B_Address[4], ~and_5_out);  // AND_Gate
  and and_9 (and_9_out, C_Address[4], ~and_6_out);  // AND_Gate
  and and_10 (and_12_out[2], and_9_out, Enable_Read);
  and and_11 (and_12_out[1], and_8_out, Enable_Write);
  and and_12 (and_12_out[0], and_7_out, Enable_Write);
  Demultiplexer #(.select(3), .width(3)) demultiplexer_1 (
    .out0(demultiplexer_1_out0), .out1(demultiplexer_1_out1), .out2(demultiplexer_1_out2),
    .out3(demultiplexer_1_out3), .out4(demultiplexer_1_out4), .out5(demultiplexer_1_out5),
    .out6(demultiplexer_1_out6), .out7(demultiplexer_1_out7), .in(and_12_out), .sel(Context_Window_Pointer));
  and and_13 (and_15_out[2], and_6_out, Enable_Read);
  and and_14 (and_15_out[1], and_5_out, Enable_Write);
  and and_15 (and_15_out[0], and_4_out, Enable_Write);
  Demultiplexer #(.select(3), .width(3)) demultiplexer_2 (
    .out0(demultiplexer_2_out0), .out1(demultiplexer_2_out1), .out2(demultiplexer_2_out2),
    .out3(demultiplexer_2_out3), .out4(demultiplexer_2_out4), .out5(demultiplexer_2_out5),
    .out6(demultiplexer_2_out6), .out7(demultiplexer_2_out7), .in(and_15_out), .sel(subtractor_1_out));
  assign Decoded_Enables = {demultiplexer_1_out7, demultiplexer_1_out6, demultiplexer_1_out5, demultiplexer_1_out4, demultiplexer_1_out3, demultiplexer_1_out2, demultiplexer_1_out1, demultiplexer_1_out0} | {demultiplexer_2_out7, demultiplexer_2_out6, demultiplexer_2_out5, demultiplexer_2_out4, demultiplexer_2_out3, demultiplexer_2_out2, demultiplexer_2_out1, demultiplexer_2_out0};  // OR_Gate or_4, 24 bits wide
  // Probe on {demultiplexer_1_out7, demultiplexer_1_out6, demultiplexer_1_out5, demultiplexer_1_out4, demultiplexer_1_out3, demultiplexer_1_out2, demultiplexer_1_out1, demultiplexer_1_out0}
  // Probe on {demultiplexer_2_out7, demultiplexer_2_out6, demultiplexer_2_out5, demultiplexer_2_out4, demultiplexer_2_out3, demultiplexer_2_out2, demultiplexer_2_out1, demultiplexer_2_out0}
  // Probe on Decoded_Enables

  // Notes on the sheet:
  //   Is lower window address?
endmodule

module Operation_Controller (
  input  [31:0] P_Bus_In,
  input  Phase2n,
  input  Phase1,
  input  Phase2,
  input  [3:0] CNZV_In,
  input  Phase3,
  input  Phase1n,
  input  Phase3n,
  input  Phase1s,
  input  Phase2s,
  input  Phase3s,
  input  Phase2i,
  input  Phase3i,
  input  Reset,
  output Set_Condition_Code,
  output Jump,
  output No_Destination,
  output Load,
  output Store,
  output Signed_Load,
  output [1:0] Data_Size,
  output [1:0] Shift_Operation,
  output Shift,
  output Load_Immediate_High,
  output ALU_Enabled,
  output [3:0] ALU_Operation,
  output Get_Last_Program_Counter,
  output Jump_Instruction,
  output Call,
  output Return_Instruction,
  output Relative,
  output Interrupt
);

  wire condition_decoder_1_always, condition_decoder_1_carry_clear, condition_decoder_1_carry_set,
       condition_decoder_1_equal, condition_decoder_1_greater, condition_decoder_1_greater_or_equal,
       condition_decoder_1_higher, condition_decoder_1_is_negative, condition_decoder_1_is_positive,
       condition_decoder_1_less, condition_decoder_1_less_or_equal, condition_decoder_1_lower_or_same,
       condition_decoder_1_never, condition_decoder_1_not_equal, condition_decoder_1_overflow_clear,
       condition_decoder_1_overflow_set, multiplexer_1_out;
  wire [3:0] CNZV_q, Condition_Code_Select_q;
  wire [6:0] Operation_Code_q;
  wire [31:0] Next_Instruction_Word_q;

  Register #(.trigger("high"), .width(32)) Next_Instruction_Word (
    .D(P_Bus_In), .en(Phase2n), .clk(Phase2n), .Q(Next_Instruction_Word_q));  // open: clr
  // Probe on CNZV_In
  Register #(.trigger("high"), .width(4)) CNZV (.D(CNZV_In), .en(Phase1), .clk(Phase1), .Q(CNZV_q));  // open: clr
  Register #(.trigger("high"), .width(7)) Operation_Code (
    .D(Next_Instruction_Word_q[6:0]), .en(Phase1), .clk(Phase1), .Q(Operation_Code_q), .clr(Reset));
  Register #(.trigger("high"), .width(1)) Set_Condition_Codes (
    .D(Next_Instruction_Word_q[7]), .en(Phase1), .clk(Phase1), .Q(Set_Condition_Code));  // open: clr
  Register #(.trigger("high"), .width(4)) Condition_Code_Select (
    .D(Next_Instruction_Word_q[11:8]), .en(Phase1), .clk(Phase1), .Q(Condition_Code_Select_q));  // open: clr
  Condition_Decoder condition_decoder_1 (
    .Carry_In(CNZV_q[0]), .Negative(CNZV_q[1]), .Zero(CNZV_q[2]), .Overflow(CNZV_q[3]),
    .Always(condition_decoder_1_always), .Never(condition_decoder_1_never),
    .Not_Equal(condition_decoder_1_not_equal), .Equal(condition_decoder_1_equal),
    .Greater(condition_decoder_1_greater), .Greater_Or_Equal(condition_decoder_1_greater_or_equal),
    .Less(condition_decoder_1_less), .Less_Or_Equal(condition_decoder_1_less_or_equal),
    .Is_Positive(condition_decoder_1_is_positive), .Is_Negative(condition_decoder_1_is_negative),
    .Higher(condition_decoder_1_higher), .Lower_Or_Same(condition_decoder_1_lower_or_same),
    .Overflow_Clear(condition_decoder_1_overflow_clear), .Overflow_Set(condition_decoder_1_overflow_set),
    .Carry_Clear(condition_decoder_1_carry_clear), .Carry_Set(condition_decoder_1_carry_set));
  Operation_Decoder operation_decoder_1 (
    .Opcode(Operation_Code_q), .No_Destination(No_Destination), .Load(Load), .Store(Store),
    .Signed_Load(Signed_Load), .Data_Size(Data_Size), .Shift_Operation(Shift_Operation), .Shift(Shift),
    .Load_Immediate_High(Load_Immediate_High), .ALU_Enable(ALU_Enabled), .ALU_Operation(ALU_Operation),
    .Get_Last_Program_Counter(Get_Last_Program_Counter), .Jump(Jump_Instruction), .Call(Call),
    .Return_Instruction(Return_Instruction), .Relative(Relative), .Interrupt(Interrupt));
  Multiplexer #(.select(4)) multiplexer_1 (
    .in0(condition_decoder_1_always), .in1(condition_decoder_1_never), .in2(condition_decoder_1_not_equal),
    .in3(condition_decoder_1_equal), .in4(condition_decoder_1_greater),
    .in5(condition_decoder_1_greater_or_equal), .in6(condition_decoder_1_less),
    .in7(condition_decoder_1_less_or_equal), .in8(condition_decoder_1_is_positive),
    .in9(condition_decoder_1_is_negative), .in10(condition_decoder_1_higher),
    .in11(condition_decoder_1_lower_or_same), .in12(condition_decoder_1_overflow_clear),
    .in13(condition_decoder_1_overflow_set), .in14(condition_decoder_1_carry_clear),
    .in15(condition_decoder_1_carry_set), .out(multiplexer_1_out), .sel(Condition_Code_Select_q));
  and and_1 (Jump, multiplexer_1_out, Jump_Instruction);
endmodule

module Window_Number_Controller (
  input  Call_Return,
  input  [31:0] LBus_In,
  input  Phi1n,
  input  Phi2n,
  output [31:0] LBus_Out,
  output Window_Overflow,
  output [2:0] Window_Number
);

  wire adder_1_cout, subtractor_1_bout, undriven;
  wire [2:0] adder_1_out, multiplexer_1_out, multiplexer_2_out, register_1_q, subtractor_1_out;

  Multiplexer #(.width(3)) multiplexer_1 (.in0(LBus_In[9:7]), .in1(register_1_q), .out(multiplexer_1_out), .sel(Phi2n));
  Register #(.trigger("high"), .width(3)) Saved_Window_Pointer (
    .D(LBus_In[6:4]), .en(undriven), .clk(undriven), .Q(LBus_Out[6:4]));  // open: clr
  Register #(.trigger("high"), .width(3)) Current_Window_Pointer (
    .D(multiplexer_1_out), .en(Phi2n), .clk(Phi2n), .Q(LBus_Out[9:7]));  // open: clr
  Adder #(.width(3)) adder_1 (.a(LBus_Out[9:7]), .b(3'b001), .out(adder_1_out), .cout(adder_1_cout));  // open: cin
  Subtractor #(.width(3)) subtractor_1 (
    .a(LBus_Out[9:7]), .b(3'b001), .out(subtractor_1_out), .bout(subtractor_1_bout));  // open: bin
  Multiplexer #(.width(3)) multiplexer_2 (
    .in0(adder_1_out), .in1(subtractor_1_out), .out(multiplexer_2_out), .sel(Call_Return));
  Multiplexer multiplexer_3 (.in0(adder_1_cout), .in1(subtractor_1_bout), .out(Window_Overflow), .sel(Call_Return));
  Register #(.trigger("high"), .width(3)) register_1 (
    .D(multiplexer_2_out), .en(Phi1n), .clk(Phi1n), .Q(register_1_q));  // open: clr

  assign Window_Number = LBus_Out[9:7];
endmodule

module Operation_Decoder (
  input  [6:0] Opcode,
  output No_Destination,
  output Load,
  output Store,
  output Signed_Load,
  output [1:0] Data_Size,
  output [1:0] Shift_Operation,
  output Shift,
  output Load_Immediate_High,
  output ALU_Enable,
  output [3:0] ALU_Operation,
  output Get_Last_Program_Counter,
  output Jump,
  output Call,
  output Return_Instruction,
  output Relative,
  output Interrupt
);

  wire and_1_out, and_2_out, and_3_out, and_4_out, and_5_out, and_8_out, and_9_out, and_10_out, and_11_out,
       and_13_out, and_14_out, and_16_out, and_17_out, and_18_out, and_20_out, and_21_out, and_22_out,
       and_23_out, and_24_out, and_25_out, and_26_out, and_27_out, and_30_out, and_31_out, and_33_out,
       and_34_out, and_35_out, and_36_out, and_37_out, and_38_out, not_1_out, not_2_out, not_3_out,
       not_4_out, not_5_out, not_6_out;

  not not_1 (not_1_out, Opcode[6]);
  not not_2 (not_2_out, Opcode[5]);
  not not_3 (not_3_out, Opcode[4]);
  not not_4 (not_4_out, Opcode[3]);
  not not_5 (not_5_out, Opcode[2]);
  not not_6 (not_6_out, Opcode[1]);
  and and_1 (and_1_out, not_1_out, not_2_out, not_3_out);
  and and_2 (and_2_out, Opcode[6], Opcode[5], not_3_out, not_4_out);
  and and_3 (and_3_out, not_1_out, Opcode[5], Opcode[4]);
  and and_4 (and_4_out, not_1_out, Opcode[5], not_3_out, Opcode[2]);
  and and_5 (and_5_out, not_1_out, Opcode[5], not_3_out, Opcode[3]);
  and and_6 (Store, not_1_out, Opcode[5], Opcode[4]);
  and and_7 (Signed_Load, not_3_out, Opcode[1]);
  and and_8 (and_8_out, not_1_out, Opcode[5], Opcode[3], not_5_out);
  and and_9 (and_9_out, not_1_out, Opcode[5], Opcode[4], Opcode[3]);
  and and_10 (and_10_out, not_1_out, Opcode[5], Opcode[3]);
  and and_11 (and_11_out, not_1_out, Opcode[5], Opcode[4], not_5_out);
  and and_12 (Shift_Operation[1], Opcode[3], Opcode[2]);
  and and_13 (and_13_out, not_1_out, not_2_out, Opcode[4], not_6_out);
  and and_14 (and_14_out, not_1_out, not_2_out, Opcode[4], Opcode[3], Opcode[2]);
  and and_15 (Load_Immediate_High, Opcode[6], Opcode[5], Opcode[4]);
  and and_16 (and_16_out, not_2_out, not_3_out);
  and and_17 (and_17_out, Opcode[6], not_4_out);
  and and_18 (and_18_out, Opcode[6], Opcode[4]);
  and and_19 (ALU_Operation[3], not_2_out, Opcode[4], not_4_out, Opcode[2]);
  and and_20 (and_20_out, not_2_out, Opcode[4]);
  and and_21 (and_21_out, Opcode[5], not_3_out);
  and and_22 (and_22_out, not_3_out, Opcode[2]);
  and and_23 (and_23_out, not_2_out, Opcode[3]);
  and and_24 (and_24_out, Opcode[5], not_3_out);
  and and_25 (and_25_out, Opcode[6], not_2_out, not_3_out, not_5_out);
  and and_26 (and_26_out, Opcode[6], not_2_out, Opcode[3], Opcode[2]);
  and and_27 (and_27_out, not_2_out, Opcode[4], not_4_out, Opcode[1]);
  and and_28 (Get_Last_Program_Counter, Opcode[6], Opcode[5], not_3_out, Opcode[3]);
  and and_29 (Jump, not_1_out, not_2_out, not_3_out, Opcode[3], Opcode[1]);
  and and_30 (and_30_out, not_1_out, not_2_out, not_3_out, not_4_out);
  and and_31 (and_31_out, not_1_out, not_2_out, not_3_out, not_6_out);
  and and_32 (Return_Instruction, Opcode[6], Opcode[5], not_3_out, not_4_out);
  and and_33 (and_33_out, not_1_out, Opcode[5], Opcode[2], Opcode[0]);
  and and_34 (and_34_out, not_1_out, Opcode[5], Opcode[3], Opcode[0]);
  and and_35 (and_35_out, not_1_out, not_2_out, not_3_out, Opcode[3], Opcode[2]);
  and and_36 (and_36_out, not_1_out, Opcode[5], Opcode[4], Opcode[0]);
  and and_37 (and_37_out, not_1_out, not_2_out, not_3_out, not_4_out);
  and and_38 (and_38_out, Opcode[6], Opcode[5], not_3_out, not_4_out, Opcode[2]);
  or or_1 (No_Destination, and_1_out, and_2_out, and_3_out);
  or or_2 (Load, and_4_out, and_5_out);
  or or_3 (Data_Size[1], and_8_out, and_9_out);
  or or_4 (Data_Size[0], and_10_out, and_11_out);
  or or_5 (Shift, and_13_out, and_14_out);
  or or_6 (ALU_Enable, and_16_out, and_17_out, and_18_out);
  or or_7 (ALU_Operation[2], not_1_out, and_20_out, and_21_out);
  or or_8 (ALU_Operation[1], not_1_out, and_22_out, and_23_out, and_24_out);
  or or_9 (ALU_Operation[0], and_25_out, and_26_out, and_27_out);
  or or_10 (Call, and_30_out, and_31_out);
  or or_11 (Relative, and_33_out, and_34_out, and_35_out, and_36_out);
  or or_12 (Interrupt, and_37_out, and_38_out);

  assign Shift_Operation[0] = Opcode[3];
endmodule

module Condition_Decoder (
  input  Carry_In,
  input  Negative,
  input  Zero,
  input  Overflow,
  output Always,
  output Never,
  output Not_Equal,
  output Equal,
  output Greater,
  output Greater_Or_Equal,
  output Less,
  output Less_Or_Equal,
  output Is_Positive,
  output Is_Negative,
  output Higher,
  output Lower_Or_Same,
  output Overflow_Clear,
  output Overflow_Set,
  output Carry_Clear,
  output Carry_Set
);

  not not_1 (Carry_Clear, Carry_In);
  not not_2 (Is_Positive, Negative);
  not not_3 (Not_Equal, Zero);
  not not_4 (Overflow_Clear, Overflow);
  or or_1 (Greater_Or_Equal, Overflow, Negative);
  and and_1 (Greater, Not_Equal, Greater_Or_Equal);
  and and_2 (Higher, Carry_In, Not_Equal);
  not not_5 (Less, Greater_Or_Equal);
  not not_6 (Less_Or_Equal, Greater);
  not not_7 (Lower_Or_Same, Higher);

  assign Always = 1'b1;
  assign Carry_Set = Carry_In;
  assign Equal = Zero;
  assign Is_Negative = Negative;
  assign Never = 1'b0;
  assign Overflow_Set = Overflow;
endmodule

module Processor_Status_Word (
  input  Set_Condition_Code,
  input  Enable_Write,
  input  Enable_Lbus_Out,
  input  [3:0] CNZV_in,
  input  [31:0] LBus_in,
  input  Reset,
  output [31:0] Lbus_out,
  output [3:0] CNZV_out
);

  wire and_1_out;
  wire [27:0] register_1_q;
  wire [31:0] multiplexer_1_out;

  Multiplexer #(.width(32)) multiplexer_1 (
    .in0(LBus_in), .in1({register_1_q, CNZV_in}), .out(multiplexer_1_out), .sel(Set_Condition_Code));
  and and_1 (and_1_out, Set_Condition_Code, Enable_Write);
  Register #(.width(32)) register_1 (
    .D(multiplexer_1_out), .en(and_1_out), .clk(and_1_out), .Q({register_1_q, CNZV_out}), .clr(Reset));
  assign Lbus_out = Enable_Lbus_Out ? {register_1_q, CNZV_out} : 32'bz;  // Controlled_Buffer controlled_buffer_1
endmodule
